# Fritzing sketch Wiring-Diagram (saved by Fritzing 0.9.3b)

parts:
  Raspberry_Pi_1 = Raspberry Pi 3 [part_number=RPI-3-V1.2]
  Door_Bell_Chime_2 = Geek Boy Door Chime  # not connected
  Door_Bell_Chime_1 = Geek Boy Door Chime

nets:
  N1: Raspberry_Pi_1.3v3, Door_Bell_Chime_1.+3V
  GND: Raspberry_Pi_1.GND, Door_Bell_Chime_1.GND

custom parts:
  Geek Boy Door Chime: Description: Door chime converted to take Raspberry Pi connections. This takes a 3 Volt, Ground and a GPIO input connection from the Raspberry Pi
